# Fritzing sketch receiver_rpi (saved by Fritzing 0.9.3b)
circuit board: 7cm x 3cm

parts:
  J1 = female pin header, 6 pins [form="♀ (female)"]
  J3 = female pin header, 6 pins [form="♀ (female)"]
  MCU2 = Raspberry Pi Zero
  J4 = female pin header, 4 pins [form="♀ (female)"]
  J5 = double row female pin header, 10 pins [form="♀ (female)"]
  J6 = female pin header, 4 pins [form="♀ (female)"]
  J7 = female pin header, 4 pins [form="♀ (female)"]  # not connected
  J8 = female pin header, 4 pins [form="♀ (female)"]  # not connected

nets:
  N1: J1.pin3, MCU2.pin_31, MCU2.pin_32
  N2: J1.pin4, J1.pin6, MCU2.pin_6, MCU2.pin_33, MCU2.pin_34, MCU2.pin_39
  N3: J1.pin5, MCU2.pin_35, MCU2.pin_36
  N4: J3.pin1, J4.pin4, J6.pin4
  N5: J3.pin2, J4.pin3, J6.pin3
  N6: J3.pin3, J4.pin2, J6.pin2
  N7: J3.pin4, J4.pin1, J6.pin1
  N8: J5.pin1, J5.pin5
  N9: J5.pin6, J5.pin7, J5.pin10

notes:
  5v
  gnd
  tx
  rx
  +
  -
  cmb87
